# Fritzing sketch fritzing-project (saved by Fritzing 0.9.6b)
breadboards: 1

parts:
  LED4 = LED - 5mm [color="Yellow (595nm)" current=30mA package="5 mm [THT]"]  # not connected
  LED6 = LED - 5mm [color="Red (660nm)" current=30mA package="5 mm [THT]"]  # not connected
  LED7 = LED - 5mm [color="Green (565nm)" current=30mA package="5 mm [THT]"]
  A1 = Raspberry Pi 5
  J1 = Buzzer
  R5 = Resistor [tolerance=±5% power=0.25W resistance=110 package=THT]
  R6 = Resistor [tolerance=±5% power=0.25W resistance=160 package=THT]
  R7 = Resistor [tolerance=±5% power=0.25W resistance=160 package=THT]

nets:
  N1: LED7.cathode, R5.Pin_0
  N2: LED7.anode, A1.GND, A1.Fan-GND, J1.pin1, R6.Pin_0
  N3: A1.GPIO17, R5.Pin_1
  N4: A1.GPIO27, R6.Pin_1
  N5: A1.GPIO22, R7.Pin_1

custom parts:
  Raspberry Pi 5: The RPi5, a faster version of the awesome Raspberry Pi4B ARM Board with 40 pin gpio.
  Buzzer: Fixed frequency buzzer
